// Logisim project pipeline.circ as structural Verilog: 4 circuits, main circuit main
module main (
  output [7:0] Non_pipelined_Out,
  output [7:0] Pipelined_Out
);

  wire CLK_out;
  wire [7:0] Address_Counter_q, rom_1_data;

  Clock CLK (.out(CLK_out));
  Counter Address_Counter (.Q(Address_Counter_q), .clk(CLK_out));  // open: load, D, count, carry, clr
  ROM rom_1 (.addr(Address_Counter_q), .data(rom_1_data));  // open: sel
  Non_pipelined Non_pipelined (.In2(8'h1), .In3(rom_1_data), .CLK(CLK_out), .Non_pipelined_Out(Non_pipelined_Out));
  Pipelined Pipelined (.In2(8'h1), .In3(rom_1_data), .CLK(CLK_out), .Pipelined_Out(Pipelined_Out));
  // Probe on Non_pipelined_Out
  // Probe on Pipelined_Out

  // Notes on the sheet:
  //   contents of rom_1 (hex, n*v repeats v):
  //   3 2 fc 1 2 fb 1
endmodule

module Non_pipelined (
  input  [7:0] In2,
  input  [7:0] In3,
  input  CLK,
  output [7:0] Non_pipelined_Out
);

  wire [7:0] adder_1_out, multiplier_1_out;

  Multiplier multiplier_1 (.a(In2), .b(In3), .out(multiplier_1_out));  // open: cin, cout
  Adder adder_1 (.a(multiplier_1_out), .b(Non_pipelined_Out), .out(adder_1_out));  // open: cin, cout
  Register N_p_Reg (.D(adder_1_out), .Q(Non_pipelined_Out), .clk(CLK));  // open: en, clr
endmodule

module Pipelined (
  input  [7:0] In2,
  input  [7:0] In3,
  input  CLK,
  output [7:0] Pipelined_Out
);

  wire [7:0] adder_1_out, multiplier_1_out, register_1_q;

  Multiplier multiplier_1 (.a(In2), .b(In3), .out(multiplier_1_out));  // open: cin, cout
  Register register_1 (.D(multiplier_1_out), .Q(register_1_q), .clk(CLK));  // open: en, clr
  Adder adder_1 (.a(register_1_q), .b(Pipelined_Out), .out(adder_1_out));  // open: cin, cout
  Register register_2 (.D(adder_1_out), .Q(Pipelined_Out), .clk(CLK));  // open: en, clr
endmodule

module fib15 (
  input  [7:0] in_1,
  output [11:0] out_2
);

  wire clock_1_out, comparator_1_lt;
  wire [7:0] adder_1_out, count_q;
  wire [11:0] adder_2_out, prev_q;

  Adder adder_1 (.a(count_q), .b(8'h1), .out(adder_1_out));  // open: cin, cout
  Register count (.D(adder_1_out), .en(1'b1), .Q(count_q), .clk(clock_1_out));  // open: clr
  // Probe on in_1
  Clock clock_1 (.out(clock_1_out));
  Comparator comparator_1 (.a(count_q), .b(in_1), .lt(comparator_1_lt));  // open: gt, eq
  Register #(.width(12)) prev (.D(out_2), .en(comparator_1_lt), .Q(prev_q), .clk(clock_1_out));  // open: clr
  Adder #(.width(12)) adder_2 (.a(out_2), .b(prev_q), .out(adder_2_out));  // open: cin, cout
  Register #(.width(12)) cur (.D(adder_2_out), .en(comparator_1_lt), .Q(out_2), .clk(clock_1_out));  // open: clr
  // Probe on out_2
endmodule
