// Logisim project cpu.circ as structural Verilog: 3 circuits, main circuit main
module main (
  input  [31:0] RS_READ_VALUE,
  input  [31:0] RT_READ_VALUE,
  input  [31:0] INSTRUCTION,
  input  CLOCK,
  output [31:0] t0,
  output [31:0] t1,
  output [31:0] t2,
  output [31:0] t3,
  output [4:0] RS,
  output [4:0] RT,
  output [4:0] Write_Register,
  output [31:0] RD_WRITE_VALUE,
  output RD_WRITE_ENABLE,
  output [23:0] FETCH_ADDRESS
);

  wire and_1_out, BRANCH, BYTE, EQUAL, IMM_t, JAL, JR, JUMP, LUI, main_2_signed_overflow, MEM_READ,
       MEM_WRITE, multiplexer_7_out, NOP, RD_REG, REGDEST, RS_REG, RT_REG, SHIFT, SIGN_EXT, SIGNED_BYTE;
  wire [1:0] multiplexer_6_out, RDReg_num, RSReg_num, RTReg_num;
  wire [4:0] multiplexer_1_out;
  wire [5:0] ALU_CTR;
  wire [7:0] bit_extender_5_out;
  wire [15:0] bit_extender_1_out, multiplexer_9_out;
  wire [23:0] adder_2_out, adder_3_out, bit_extender_4_out, bit_extender_9_out, bit_extender_10_out,
       multiplexer_14_out, multiplexer_18_out, multiplexer_19_out, PC, PC_1;
  wire [31:0] bit_extender_3_out, bit_extender_6_out, bit_extender_7_out, bit_extender_8_out, CURR_OP, IMM32,
       main_1_read_data_1, main_1_read_data_2, main_2_result, main_3_data_mem_out, multiplexer_5_out,
       multiplexer_8_out, multiplexer_10_out, multiplexer_11_out, multiplexer_13_out, multiplexer_15_out,
       multiplexer_16_out, PC32, Result, subtractor_2_out, x;

  Multiplexer #(.width(5), .enable("false")) multiplexer_1 (
    .in0(RT), .in1(CURR_OP[15:11]), .out(multiplexer_1_out), .sel(REGDEST));
  Multiplexer #(.width(5), .enable("false")) multiplexer_2 (
    .in0(multiplexer_1_out), .in1({5{1'b1}}), .out(Write_Register), .sel(JAL));
  Multiplexer #(.width(32), .enable("false")) multiplexer_3 (.in0(Result), .in1(PC32), .out(RD_WRITE_VALUE), .sel(JAL));
  Multiplexer #(.width(24), .enable("false")) multiplexer_4 (.in0(PC), .in1(PC_1), .out(FETCH_ADDRESS), .sel(NOP));
  RegDest regdest_1 (.RegIn(RS), .Reg_File_Addr(RSReg_num), .Is_t0_t4(RS_REG));
  RegDest regdest_2 (.RegIn(RT), .Reg_File_Addr(RTReg_num), .Is_t0_t4(RT_REG));
  RegDest regdest_3 (.RegIn(CURR_OP[15:11]), .Reg_File_Addr(RDReg_num), .Is_t0_t4(RD_REG));
  Multiplexer #(.width(32), .enable("false")) multiplexer_5 (
    .in0(INSTRUCTION), .in1({32{1'b0}}), .out(multiplexer_5_out), .sel(NOP));
  Register #(.width(32)) register_1 (
    .D(multiplexer_5_out), .Q({CURR_OP[31:26], RS, RT, CURR_OP[15:0]}), .clk(CLOCK));  // open: en, clr
  Multiplexer #(.width(2), .enable("false")) multiplexer_6 (
    .in0(RTReg_num), .in1(RDReg_num), .out(multiplexer_6_out), .sel(REGDEST));
  Multiplexer #(.enable("false")) multiplexer_7 (.in0(RT_REG), .in1(RD_REG), .out(multiplexer_7_out), .sel(REGDEST));
  Control control_1 (
    .EQUAL(EQUAL), .OPCODE(CURR_OP[31:26]), .FUNCT(CURR_OP[5:0]), .REGDEST(REGDEST), .IMMEDIATE(IMM_t),
    .MEMREAD(MEM_READ), .BYTE(BYTE), .SIGNED_BYTE(SIGNED_BYTE), .REGWRITE(RD_WRITE_ENABLE),
    .MEMWRITE(MEM_WRITE), .BRANCH(BRANCH), .JUMP(JUMP), .JAL(JAL), .JR(JR), .SIGN_EXTEND(SIGN_EXT),
    .SHIFT(SHIFT), .LUI(LUI), .ALU_CTRL(ALU_CTR));
  regfile_main main_1 (
    .Read_register_1(RSReg_num), .Read_register_2(RTReg_num), .write_register(multiplexer_6_out),
    .write_data(Result), .t0_Value(t0), .t1_Value(t1), .t2_Value(t2), .t3_Value(t3), .RegWrite(and_1_out),
    .clock(CLOCK), .Read_Data_1(main_1_read_data_1), .Read_Data_2(main_1_read_data_2));
  and and_1 (and_1_out, multiplexer_7_out, RD_WRITE_ENABLE);
  assign bit_extender_1_out = {{11{1'b0}}, CURR_OP[10:6]};  // Bit_Extender bit_extender_1
  Multiplexer #(.width(32), .enable("false")) multiplexer_8 (
    .in0(RS_READ_VALUE), .in1(main_1_read_data_1), .out(multiplexer_8_out), .sel(RS_REG));
  Multiplexer #(.width(16), .enable("false")) multiplexer_9 (
    .in0(CURR_OP[15:0]), .in1(bit_extender_1_out), .out(multiplexer_9_out), .sel(SHIFT));
  Multiplexer #(.width(32), .enable("false")) multiplexer_10 (
    .in0(RT_READ_VALUE), .in1(main_1_read_data_2), .out(multiplexer_10_out), .sel(RT_REG));
  assign IMM32 = {{16{1'b0}}, multiplexer_9_out};  // Bit_Extender bit_extender_2
  Multiplexer #(.width(32), .enable("false")) multiplexer_11 (
    .in0(IMM32), .in1(bit_extender_3_out), .out(multiplexer_11_out), .sel(SIGN_EXT));
  assign bit_extender_3_out = {{16{multiplexer_9_out[15]}}, multiplexer_9_out};  // Bit_Extender bit_extender_3
  // Probe on multiplexer_18_out
  Multiplexer #(.select(2), .width(32), .enable("false")) multiplexer_12 (
    .in0(multiplexer_8_out), .in1(IMM32), .in2(multiplexer_10_out), .out(x), .sel({SHIFT, LUI}));  // open: in3
  alu_main main_2 (
    .Switch__S(ALU_CTR), .X(x), .Equal(EQUAL), .RESULT(main_2_result),
    .Signed_Overflow(main_2_signed_overflow), .Y(multiplexer_13_out));
  Multiplexer #(.width(32), .enable("false")) multiplexer_13 (
    .in0(multiplexer_10_out), .in1(multiplexer_15_out), .out(multiplexer_13_out), .sel(IMM_t));
  Multiplexer #(.width(24), .enable("false")) multiplexer_14 (
    .in0(multiplexer_18_out), .in1(bit_extender_4_out), .out(multiplexer_14_out), .sel(JR));
  Bit_Extender #(.in_width(32), .out_width(24)) bit_extender_4 (.in(x), .out(bit_extender_4_out));
  or or_1 (NOP, BRANCH, JUMP, JAL, JR);
  LED Signed_Overflow (.in(main_2_signed_overflow));
  Multiplexer #(.width(32), .enable("false")) multiplexer_15 (
    .in0(multiplexer_11_out), .in1(32'h10), .out(multiplexer_15_out), .sel(LUI));
  Register #(.width(24)) u_PC (.D(multiplexer_14_out), .Q(PC), .clk(CLOCK));  // open: en, clr
  mem_main main_3 (
    .Data_Mem_Addr(main_2_result), .Data_Mem_In(multiplexer_10_out), .ACCESS_BYTE(BYTE),
    .MEM_WRITE(MEM_WRITE), .CLOCK(CLOCK), .Data_Mem_Out(main_3_data_mem_out));
  Bit_Extender #(.in_width(32), .out_width(8)) bit_extender_5 (.in(main_3_data_mem_out), .out(bit_extender_5_out));
  assign bit_extender_6_out = {{8{1'b0}}, PC};  // Bit_Extender bit_extender_6
  Multiplexer #(.width(32), .enable("false")) multiplexer_16 (
    .in0(main_3_data_mem_out), .in1(bit_extender_7_out), .out(multiplexer_16_out), .sel(SIGNED_BYTE));
  assign bit_extender_7_out = {{24{bit_extender_5_out[7]}}, bit_extender_5_out};  // Bit_Extender bit_extender_7
  Adder #(.width(32)) adder_1 (.a({32{1'b0}}), .b(bit_extender_6_out), .out(PC32));  // open: cin, cout
  Subtractor #(.width(24)) subtractor_1 (.a(PC), .b(24'h1), .out(PC_1));  // open: bin, bout
  Adder #(.width(24)) adder_2 (.a(24'h1), .b(PC), .out(adder_2_out));  // open: cin, cout
  assign bit_extender_8_out = {{6{1'b0}}, {RS, RT, CURR_OP[15:0]}};  // Bit_Extender bit_extender_8
  Multiplexer #(.width(32), .enable("false")) multiplexer_17 (
    .in0(main_2_result), .in1(multiplexer_16_out), .out(Result), .sel(MEM_READ));
  Adder #(.width(24)) adder_3 (.a(PC), .b(bit_extender_9_out), .out(adder_3_out));  // open: cin, cout
  assign bit_extender_9_out = {{8{CURR_OP[15]}}, CURR_OP[15:0]};  // Bit_Extender bit_extender_9
  Multiplexer #(.width(24), .enable("false")) multiplexer_18 (
    .in0(multiplexer_19_out), .in1(bit_extender_10_out), .out(multiplexer_18_out), .sel(JUMP));
  Subtractor #(.width(32)) subtractor_2 (
    .a(bit_extender_8_out), .b(32'h40100000), .out(subtractor_2_out));  // open: bin, bout
  Bit_Extender #(.in_width(32), .out_width(24)) bit_extender_10 (.in(subtractor_2_out), .out(bit_extender_10_out));
  Multiplexer #(.width(24), .enable("false")) multiplexer_19 (
    .in0(adder_2_out), .in1(adder_3_out), .out(multiplexer_19_out), .sel(BRANCH));

  // Other names for the same wires on the sheet: CLK = CLOCK; FUNCT[5:0] = CURR_OP[5:0]; IMM[15:0] = CURR_OP[15:0];
  //   JADDR[25:0] = {RS, RT, CURR_OP[15:0]}; SHAMT[4:0] = CURR_OP[10:6]; RD[4:0] = CURR_OP[15:11];
  //   CURR_OP[25:16] = {RS, RT}; OPCODE[5:0] = CURR_OP[31:26]; REGWRITE = RD_WRITE_ENABLE;
  //   RS_Read[31:0] = RS_READ_VALUE; RT_Read[31:0] = RT_READ_VALUE

  // Notes on the sheet:
  //   These are outputs/inputs from run.circ
  //   These are outputs to run.circ
endmodule

module RegDest (
  input  [4:0] RegIn,
  output [1:0] Reg_File_Addr,
  output Is_t0_t4
);

  wire not_1_out, not_2_out;

  not not_1 (not_1_out, RegIn[2]);
  and and_1 (Is_t0_t4, not_1_out, RegIn[3], not_2_out);
  not not_2 (not_2_out, RegIn[4]);

  assign Reg_File_Addr = RegIn[1:0];
endmodule

// CONTROL
module Control (
  input  EQUAL,
  input  [5:0] OPCODE,
  input  [5:0] FUNCT,
  output REGDEST,
  output IMMEDIATE,
  output MEMREAD,
  output BYTE,
  output SIGNED_BYTE,
  output REGWRITE,
  output MEMWRITE,
  output BRANCH,
  output JUMP,
  output JAL,
  output JR,
  output SIGN_EXTEND,
  output SHIFT,
  output LUI,
  output [5:0] ALU_CTRL
);

  wire and_1_out, and_2_out, and_3_out, BranchInstr, comparator_1_eq, comparator_3_eq, comparator_4_eq,
       comparator_7_eq, comparator_8_eq, comparator_9_eq, comparator_11_eq, comparator_13_eq,
       comparator_14_eq, comparator_15_eq, comparator_17_eq, comparator_18_eq, comparator_19_eq,
       comparator_20_eq, comparator_21_eq, comparator_22_eq, nor_1_out, not_1_out, not_2_out, not_3_out,
       or_3_out, or_5_out, or_6_out, or_7_out, or_8_out, or_9_out;
  wire [5:0] multiplexer_1_out, multiplexer_2_out, multiplexer_3_out;

  Multiplexer #(.width(6), .enable("false")) multiplexer_1 (
    .in0({6{1'b0}}), .in1(6'b100101), .out(multiplexer_1_out), .sel(comparator_1_eq));
  Comparator #(.width(6)) comparator_1 (.a(6'b001101), .b(OPCODE), .eq(comparator_1_eq));  // open: gt, lt
  Comparator #(.width(6)) comparator_2 (.a({6{1'b0}}), .b(OPCODE), .eq(REGDEST));  // open: gt, lt
  not not_1 (not_1_out, REGDEST);
  and and_1 (and_1_out, not_1_out, not_2_out);
  not not_2 (not_2_out, BranchInstr);
  Comparator #(.width(6)) comparator_3 (.a(6'b100011), .b(OPCODE), .eq(comparator_3_eq));  // open: gt, lt
  Comparator #(.width(6)) comparator_4 (.a(6'b100100), .b(OPCODE), .eq(comparator_4_eq));  // open: gt, lt
  Comparator #(.width(6)) comparator_5 (.a(6'b100000), .b(OPCODE), .eq(SIGNED_BYTE));  // open: gt, lt
  Comparator #(.width(6)) comparator_6 (.a(6'b101011), .b(OPCODE), .eq(MEMWRITE));  // open: gt, lt
  Comparator #(.width(6)) comparator_7 (.a(6'b000100), .b(OPCODE), .eq(comparator_7_eq));  // open: gt, lt
  Comparator #(.width(6)) comparator_8 (.a(6'b000101), .b(OPCODE), .eq(comparator_8_eq));  // open: gt, lt
  Comparator #(.width(6)) comparator_9 (.a(6'b000010), .b(OPCODE), .eq(comparator_9_eq));  // open: gt, lt
  Comparator #(.width(6)) comparator_10 (.a(6'b000011), .b(OPCODE), .eq(JAL));  // open: gt, lt
  Comparator #(.width(6)) comparator_11 (.a(6'b001000), .b(FUNCT), .eq(comparator_11_eq));  // open: gt, lt
  Comparator #(.width(6)) comparator_12 (.a(6'b001001), .b(OPCODE), .eq(SIGN_EXTEND));  // open: gt, lt
  Comparator #(.width(6)) comparator_13 (.a({6{1'b0}}), .b(FUNCT), .eq(comparator_13_eq));  // open: gt, lt
  Comparator #(.width(6)) comparator_14 (.a(6'b000010), .b(FUNCT), .eq(comparator_14_eq));  // open: gt, lt
  Comparator #(.width(6)) comparator_15 (.a(6'b000011), .b(FUNCT), .eq(comparator_15_eq));  // open: gt, lt
  Comparator #(.width(6)) comparator_16 (.a(6'b001111), .b(OPCODE), .eq(LUI));  // open: gt, lt
  Multiplexer #(.width(6), .enable("false")) multiplexer_2 (
    .in0(multiplexer_1_out), .in1(6'b100100), .out(multiplexer_2_out), .sel(comparator_17_eq));
  Comparator #(.width(6)) comparator_17 (.a(6'b001100), .b(OPCODE), .eq(comparator_17_eq));  // open: gt, lt
  or or_1 (IMMEDIATE, SHIFT, and_1_out);
  or or_2 (MEMREAD, comparator_3_eq, comparator_4_eq, SIGNED_BYTE);
  or or_3 (or_3_out, REGDEST, IMMEDIATE);
  or or_4 (BranchInstr, comparator_7_eq, comparator_8_eq);
  not not_3 (not_3_out, EQUAL);
  or or_5 (or_5_out, comparator_13_eq, comparator_14_eq, comparator_15_eq);
  Multiplexer #(.width(6), .enable("false")) multiplexer_3 (
    .in0(multiplexer_2_out), .in1(6'b100001), .out(multiplexer_3_out), .sel(or_6_out));
  Comparator #(.width(6)) comparator_18 (.a(6'b001001), .b(OPCODE), .eq(comparator_18_eq));  // open: gt, lt
  or or_6 (or_6_out, comparator_18_eq, or_7_out);
  or or_7 (or_7_out, comparator_19_eq, or_8_out);
  Comparator #(.width(6)) comparator_19 (.a(6'b100011), .b(OPCODE), .eq(comparator_19_eq));  // open: gt, lt
  or or_8 (or_8_out, comparator_20_eq, or_9_out);
  Comparator #(.width(6)) comparator_20 (.a(6'b100100), .b(OPCODE), .eq(comparator_20_eq));  // open: gt, lt
  or or_9 (or_9_out, comparator_21_eq, comparator_22_eq);
  Comparator #(.width(6)) comparator_21 (.a(6'b100000), .b(OPCODE), .eq(comparator_21_eq));  // open: gt, lt
  Comparator #(.width(6)) comparator_22 (.a(6'b101011), .b(OPCODE), .eq(comparator_22_eq));  // open: gt, lt
  or or_10 (BYTE, comparator_4_eq, SIGNED_BYTE);
  nor nor_1 (nor_1_out, BranchInstr, JR, MEMWRITE);
  and and_2 (and_2_out, EQUAL, comparator_7_eq);
  or or_11 (BRANCH, and_2_out, and_3_out);
  and and_3 (and_3_out, comparator_8_eq, not_3_out);
  or or_12 (JUMP, comparator_9_eq, JAL);
  and and_4 (JR, comparator_11_eq, REGDEST);
  and and_5 (SHIFT, or_5_out, REGDEST);
  Multiplexer #(.width(6), .enable("false")) multiplexer_4 (
    .in0(multiplexer_3_out), .in1(FUNCT), .out(ALU_CTRL), .sel(REGDEST));
  and and_6 (REGWRITE, or_3_out, nor_1_out);
endmodule
