// Logisim project alu.circ as structural Verilog: 5 circuits, main circuit main
module main (
  input  [31:0] X,
  input  [31:0] Y,
  input  [5:0] Switch__S,
  output Signed_Overflow,
  output [31:0] RESULT,
  output Equal
);

  wire CarryIn, CarryOut, CHK_OVF, comparator_1_lt, comparator_2_lt, xor_1_out;
  wire [4:0] yBottom5;
  wire [31:0] addsub, \and , bitpal, lfsr, multiplexer_1_out, multiplexer_2_out, multiplexer_3_out,
       multiplexer_4_out, multiplexer_5_out, multiplexer_6_out, multiplexer_7_out, not_1_out, \or , sll, slt,
       sltu, sra, srl;

  Bit_Extender #(.in_width(32), .out_width(5)) bit_extender_1 (.in(Y), .out(yBottom5));
  Subtraction_Detector subtraction_detector_1 (.FUNCT(Switch__S), .SUB(CarryIn));
  Overflow_Checker overflow_checker_1 (.FUNCT(Switch__S), .CHK_OVF(CHK_OVF));
  Shifter #(.width(32)) shifter_1 (.in(X), .\dist (yBottom5), .out(sll));
  Shifter #(.width(32), .shift("lr")) shifter_2 (.in(X), .\dist (yBottom5), .out(srl));
  Shifter #(.width(32), .shift("ar")) shifter_3 (.in(X), .\dist (yBottom5), .out(sra));
  Comparator #(.width(32)) comparator_1 (.a(X), .b(Y), .eq(Equal), .lt(comparator_1_lt));  // open: gt
  Comparator #(.width(32), .mode("unsigned")) comparator_2 (.a(X), .b(Y), .lt(comparator_2_lt));  // open: gt, eq
  assign \and  = X & Y;  // AND_Gate and_1, 32 bits wide
  assign \or  = X | Y;  // OR_Gate or_1, 32 bits wide
  BITPAL bitpal_1 (.X(X), .BITPAL(bitpal));
  LFSR lfsr_1 (.X(X), .LFSR(lfsr));
  assign not_1_out = ~Y;  // NOT_Gate not_1, 32 bits wide
  assign sltu = {{31{1'b0}}, comparator_2_lt};  // Bit_Extender bit_extender_2
  Adder #(.width(32)) adder_1 (.a(X), .b(multiplexer_1_out), .out(addsub), .cin(CarryIn), .cout(CarryOut));
  Multiplexer #(.width(32), .enable("false")) multiplexer_1 (
    .in0(Y), .in1(not_1_out), .out(multiplexer_1_out), .sel(CarryIn));
  assign slt = {{31{1'b0}}, comparator_1_lt};  // Bit_Extender bit_extender_3
  Multiplexer #(.width(32), .enable("false")) multiplexer_2 (
    .in0(\and ), .in1(\or ), .out(multiplexer_2_out), .sel(Switch__S[0]));
  Multiplexer #(.width(32), .enable("false")) multiplexer_3 (
    .in0(slt), .in1(sltu), .out(multiplexer_3_out), .sel(Switch__S[0]));
  Multiplexer #(.width(32), .enable("false")) multiplexer_4 (
    .in0(bitpal), .in1(lfsr), .out(multiplexer_4_out), .sel(Switch__S[0]));
  Multiplexer #(.select(2), .width(32), .enable("false")) multiplexer_5 (
    .in0(sll), .in2(srl), .in3(sra), .out(multiplexer_5_out), .sel(Switch__S[1:0]));  // open: in1
  Multiplexer #(.width(32), .enable("false")) multiplexer_6 (
    .in0(addsub), .in1(multiplexer_2_out), .out(multiplexer_6_out), .sel(Switch__S[2]));
  Multiplexer #(.width(32), .enable("false")) multiplexer_7 (
    .in0(multiplexer_6_out), .in1(multiplexer_3_out), .out(multiplexer_7_out), .sel(Switch__S[3]));
  Multiplexer #(.enable("false")) multiplexer_8 (.in0(1'b0), .in1(xor_1_out), .out(Signed_Overflow), .sel(CHK_OVF));
  xor xor_1 (xor_1_out, CarryIn, CarryOut);
  Multiplexer #(.select(2), .width(32), .enable("false")) multiplexer_9 (
    .in0(multiplexer_5_out), .in2(multiplexer_7_out), .in3(multiplexer_4_out), .out(RESULT),
    .sel(Switch__S[5:4]));  // open: in1

  // Other names for the same wires on the sheet: S[5:0] = Switch__S; SBottom2Bits[1:0] = Switch__S[1:0];
  //   SBottomBit = Switch__S[0]; S3rdBit = Switch__S[2]; S4thBit = Switch__S[3]; STop2Bits[1:0] = Switch__S[5:4];
  //   SUB = CarryIn

  // Notes on the sheet:
  //   INPUTS to your circuit
  //   INPUT to your circuit
  //   DON'T CHANGE THE INPUTS AND OUTPUTS! IF YOU DO SO, YOU NEED TO MAKE SURE THE PINS ARE IN THE RIGHT PLACES!
  //   OUTPUTS of your circuit
endmodule

module Subtraction_Detector (
  input  [5:0] FUNCT,
  output SUB
);

  wire comparator_1_eq, comparator_2_eq;

  Comparator #(.width(6)) comparator_1 (.a(FUNCT), .b(6'b100010), .eq(comparator_1_eq));  // open: gt, lt
  Comparator #(.width(6)) comparator_2 (.a(FUNCT), .b(6'b100011), .eq(comparator_2_eq));  // open: gt, lt
  or or_1 (SUB, comparator_1_eq, comparator_2_eq);

  // Notes on the sheet:
  //   Determines if the funct is a subtraction
  //   1 if funct is a subtraction
  //   0 otherwise
endmodule

module Overflow_Checker (
  input  [5:0] FUNCT,
  output CHK_OVF
);

  wire comparator_1_eq, comparator_2_eq;

  Comparator #(.width(6)) comparator_1 (.a(FUNCT), .b(6'b100000), .eq(comparator_1_eq));  // open: gt, lt
  Comparator #(.width(6)) comparator_2 (.a(FUNCT), .b(6'b100010), .eq(comparator_2_eq));  // open: gt, lt
  or or_1 (CHK_OVF, comparator_1_eq, comparator_2_eq);

  // Notes on the sheet:
  //   Determines based on the funct whether we need to check for overflow or not
  //   0 otherwise
  //   1 if overflow checking needed
endmodule

module LFSR (
  input  [31:0] X,
  output [31:0] LFSR
);

  wire xor_1_out, xor_2_out;
  wire [31:0] shifter_1_out;

  xor xor_1 (xor_1_out, X[0], X[2]);
  xor xor_2 (xor_2_out, xor_1_out, X[3]);
  xor xor_3 (LFSR[31], xor_2_out, X[5]);
  Shifter #(.width(32), .shift("lr")) shifter_1 (.in(X), .\dist (5'b00001), .out(shifter_1_out));
  Bit_Extender #(.in_width(32), .out_width(31)) bit_extender_1 (.in(shifter_1_out), .out(LFSR[30:0]));
endmodule

module BITPAL (
  input  [31:0] X,
  output [31:0] BITPAL
);

  wire comparator_1_eq;

  Comparator #(.width(16)) comparator_1 (
    .a({X[0], X[1], X[2], X[3], X[4], X[5], X[6], X[7], X[8], X[9], X[10], X[11], X[12], X[13], X[14], X[15]}),
    .b(X[31:16]), .eq(comparator_1_eq));  // open: gt, lt
  assign BITPAL = {{31{1'b0}}, comparator_1_eq};  // Bit_Extender bit_extender_1
endmodule
