// Logisim project mem.circ as structural Verilog: 2 circuits, main circuit main
module main (
  input  [31:0] Data_Mem_Addr,
  input  [31:0] Data_Mem_In,
  input  ACCESS_BYTE,
  input  MEM_WRITE,
  input  CLOCK,
  output [31:0] Data_Mem_Out
);

  wire not_1_out;
  wire [23:0] bit_extender_1_out;
  wire [31:0] BasedAddr, byte_value_calculator_1_output, controlled_buffer_1_out, Mem_Out, shifter_1_out;

  Subtractor #(.width(32)) subtractor_1 (.a(Data_Mem_Addr), .b(32'h90), .out(BasedAddr));  // open: bin, bout
  Shifter #(.width(32), .shift("lr")) shifter_1 (.in(BasedAddr), .\dist (5'b00010), .out(shifter_1_out));
  Bit_Extender #(.in_width(32), .out_width(24)) bit_extender_1 (.in(shifter_1_out), .out(bit_extender_1_out));
  not not_1 (not_1_out, MEM_WRITE);
  assign controlled_buffer_1_out = MEM_WRITE ? Data_Mem_In : 32'bz;  // Controlled_Buffer controlled_buffer_1
  RAM #(.addrWidth(24), .dataWidth(32)) ram_1 (
    .addr(bit_extender_1_out), .data(controlled_buffer_1_out), .sel(1'b1), .clk(CLOCK), .ld(not_1_out));  // open: clr
  Byte_Value_Calculator byte_value_calculator_1 (
    .Word_Value(controlled_buffer_1_out), .Based_Addr(BasedAddr), .Output(byte_value_calculator_1_output));
  Multiplexer #(.width(32), .enable("false")) multiplexer_1 (
    .in0(Mem_Out), .in1(Data_Mem_In), .out(Data_Mem_Out), .sel(MEM_WRITE));
  Multiplexer #(.width(32), .enable("false")) multiplexer_2 (
    .in0(controlled_buffer_1_out), .in1(byte_value_calculator_1_output), .out(Mem_Out), .sel(ACCESS_BYTE));

  // Other names for the same wires on the sheet: CLK = CLOCK; Mem_In[31:0] = Data_Mem_In

  // Notes on the sheet:
  //   These are INPUTS to the circuit
  //   These are INPUTS to the circuit
  //   DO NOT CHANGE THE LOCATIONS OF THE INPUTS/OUTPUTS! IF YOU DO SO, YOU NEED TO MAKE SURE THE PINS ARE AT THE RIGHT PLACE!
  //   Yet again, the clock is not an actual clock, but an input, one that will be driven from a higher circuit
  //   This is an OUTPUT to the circuit
endmodule

module Byte_Value_Calculator (
  input  [31:0] Word_Value,
  input  [31:0] Based_Addr,
  output [31:0] Output
);

  wire [1:0] Byte_Offset;
  wire [4:0] multiplexer_1_out;
  wire [31:0] shifter_1_out;

  Multiplexer #(.select(2), .width(5), .enable("false")) multiplexer_1 (
    .in0(5'b11000), .in1(5'b10000), .in2(5'b01000), .in3({5{1'b0}}), .out(multiplexer_1_out),
    .sel(Byte_Offset));
  Bit_Extender #(.in_width(32), .out_width(2)) bit_extender_1 (.in(Based_Addr), .out(Byte_Offset));
  Shifter #(.width(32), .shift("lr")) shifter_1 (.in(Word_Value), .\dist (multiplexer_1_out), .out(shifter_1_out));
  assign Output = 32'hff & shifter_1_out;  // AND_Gate and_1, 32 bits wide
endmodule
