// Logisim project regfile.circ as structural Verilog: 1 circuit, main circuit main
module main (
  input  [1:0] Read_register_1,
  input  [1:0] Read_register_2,
  input  [1:0] write_register,
  input  [31:0] write_data,
  input  RegWrite,
  input  clock,
  output [31:0] t0_Value,
  output [31:0] t1_Value,
  output [31:0] t2_Value,
  output [31:0] t3_Value,
  output [31:0] Read_Data_1,
  output [31:0] Read_Data_2
);

  wire Write0, Write1, Write2, Write3;
  wire [31:0] multiplexer_1_out, multiplexer_2_out, multiplexer_3_out, multiplexer_4_out;

  Demultiplexer #(.select(2), .enable("false")) demultiplexer_1 (
    .out0(Write0), .out1(Write1), .out2(Write2), .out3(Write3), .in(RegWrite), .sel(write_register));
  Multiplexer #(.width(32), .enable("false")) multiplexer_1 (
    .in0(t0_Value), .in1(write_data), .out(multiplexer_1_out), .sel(Write0));
  Register #(.width(32)) t0write (.D(multiplexer_1_out), .Q(t0_Value), .clk(clock));  // open: en, clr
  Register #(.width(32)) t1write (.D(multiplexer_2_out), .Q(t1_Value), .clk(clock));  // open: en, clr
  Multiplexer #(.width(32), .enable("false")) multiplexer_2 (
    .in0(t1_Value), .in1(write_data), .out(multiplexer_2_out), .sel(Write1));
  Register #(.width(32)) t2write (.D(multiplexer_3_out), .Q(t2_Value), .clk(clock));  // open: en, clr
  Multiplexer #(.width(32), .enable("false")) multiplexer_3 (
    .in0(t2_Value), .in1(write_data), .out(multiplexer_3_out), .sel(Write2));
  Register #(.width(32)) t3write (.D(multiplexer_4_out), .Q(t3_Value), .clk(clock));  // open: en, clr
  Multiplexer #(.width(32), .enable("false")) multiplexer_4 (
    .in0(t3_Value), .in1(write_data), .out(multiplexer_4_out), .sel(Write3));
  Multiplexer #(.select(2), .width(32), .enable("false")) multiplexer_5 (
    .in0(t0_Value), .in1(t1_Value), .in2(t2_Value), .in3(t3_Value), .out(Read_Data_1), .sel(Read_register_1));
  Multiplexer #(.select(2), .width(32), .enable("false")) multiplexer_6 (
    .in0(t0_Value), .in1(t1_Value), .in2(t2_Value), .in3(t3_Value), .out(Read_Data_2), .sel(Read_register_2));

  // Other names for the same wires on the sheet: CLK = clock; ReadReg1[1:0] = Read_register_1;
  //   ReadReg2[1:0] = Read_register_2; t0[31:0] = t0_Value; t0_read[31:0] = t0_Value; t1[31:0] = t1_Value;
  //   t1_read[31:0] = t1_Value; t2[31:0] = t2_Value; t2_read[31:0] = t2_Value; t3[31:0] = t3_Value;
  //   t3_read[31:0] = t3_Value; WriteData[31:0] = write_data; WriteReg[1:0] = write_register

  // Notes on the sheet:
  //   These are INPUTS to the circuit
  //   These are INPUTS to the circuit
  //   DO NOT CHANGE THE LOCATIONS OF THE INPUTS/OUTPUTS! IF YOU DO SO, YOU NEED TO MAKE SURE THE PINS ARE AT THE RIGHT PLACE!
  //   These are OUTPUTS to the circuit
  //   Yet again, the clock is not an actual clock, but an input, one that will be driven from a higher circuit
  //   These are OUTPUTS to the circuit
endmodule
